// Logisim project alu.circ as structural Verilog: 1 circuit, main circuit ALU
module ALU (
  input  [31:0] A,
  input  [31:0] B,
  input  [3:0] ALU_Op,
  output [31:0] Out
);

  wire [31:0] ADD, And, Div, divider_2_out, Mul, OR, SLL, SLR, SLT, SRL, SUB, undriven, undriven_2, XOR;

  Shifter #(.width(32)) shifter_1 (.in(A), .\dist (B[4:0]), .out(SLL));
  Shifter #(.width(32), .shift("lr")) shifter_2 (.in(A), .\dist (B[4:0]), .out(SRL));
  Multiplier #(.width(32)) multiplier_1 (.a(A), .b(B), .out(Mul));  // open: cin, cout
  Comparator #(.width(32)) comparator_1 (.a(A), .b(B), .eq(SLT[0]));  // open: gt, lt
  Divider #(.width(32)) divider_1 (.a(A), .b(B), .out(Div));  // open: upper, rem
  Divider #(.width(32)) divider_2 (.a(A), .b(B), .out(divider_2_out));  // open: upper, rem
  assign And = A & B;  // AND_Gate and_1, 32 bits wide
  assign OR = A | B;  // OR_Gate or_1, 32 bits wide
  assign XOR = A ^ B;  // XOR_Gate xor_1, 32 bits wide
  Adder #(.width(32)) adder_1 (.a(A), .b(B), .out(ADD));  // open: cin, cout
  Subtractor #(.width(32)) subtractor_1 (.a(A), .b(B), .out(SUB));  // open: bin, bout
  Multiplexer #(.select(4), .width(32)) multiplexer_1 (
    .in0(ADD), .in1(SUB), .in2(SLT), .in3(Mul), .in4(SLL), .in5(SLR), .in6(Div), .in7(undriven),
    .in8(undriven_2), .in9(And), .in10(OR), .in11(XOR), .out(Out), .sel(ALU_Op));  // open: in12, in13, in14, in15, en

  // Other names for the same wires on the sheet: s2_5min[4:0] = B[4:0]; Op[3:0] = ALU_Op

  // Notes on the sheet:
  //   Inputs
  //   NOTE
  //   Please do not modify/replace/move/change/delete/etc input and output pins
  //   Outputs
endmodule
