// Logisim project cpu.circ as structural Verilog: 4 circuits, main circuit CPU
module CPU (
  input  [31:0] Instruction,
  input  CLK,
  output [31:0] s0,
  output [31:0] s1,
  output [31:0] t0,
  output [31:0] t1,
  output [31:0] a0,
  output [31:0] ra,
  output [31:0] sp,
  output [31:0] PC
);

  wire ALUSEL, B, J, MEMR, MEMSEL, MEMW, or_1_out, WE;
  wire [3:0] op;
  wire [31:0] alu_1_out, IMM, incrementer_1_p2, incrementer_1_p3, main_1_p5, multiplexer_2_out,
       multiplexer_3_out, PC_IMM, PC_t, regfile_1_r1, regfile_1_r2;

  // Incrementer incrementer_1: pin names not known; wires that end beside it: PC_t, incrementer_1_p2, incrementer_1_p3
  Multiplexer #(.width(32), .enable("false")) multiplexer_1 (
    .in0(incrementer_1_p2), .in1(PC_IMM), .out(incrementer_1_p3), .sel(or_1_out));
  or or_1 (or_1_out, J, B);
  // Probe on Instruction[14:12]
  // Probe on Instruction[6:0]
  // Probe on Instruction[31:25]
  Adder #(.width(32)) adder_1 (.a(PC_t), .b(IMM), .out(PC_IMM));  // open: cin, cout
  // PC pc_1: pin names not known; wires that end beside it: CLK, PC_t
  // Probe on Instruction[6:0]
  RegFile regfile_1 (
    .Clk(CLK), .R1(regfile_1_r1), .R2(regfile_1_r2), .WE(WE), .W(multiplexer_3_out), .RD(Instruction[11:7]),
    .RS1(Instruction[19:15]), .RS2(Instruction[24:20]), .s0(s0), .s1(s1), .t0(t0), .t1(t1), .a0(a0), .ra(ra),
    .sp(sp));
  Multiplexer #(.width(32), .enable("false")) multiplexer_2 (
    .in0(regfile_1_r2), .in1(IMM), .out(multiplexer_2_out), .sel(ALUSEL));
  GeneradorImm generadorimm_1 (.INST(Instruction), .Opcode(Instruction[6:0]), .Imm(IMM));
  Control control_1 (
    .Opcode(Instruction[6:0]), .RegW(WE), .AluSel(ALUSEL), .MemW(MEMW), .MemR(MEMR), .MemSel(MEMSEL),
    .Branch(B), .Jump(J));
  ALU alu_1 (.A(regfile_1_r1), .B(multiplexer_2_out), .ALU_Op(op), .Out(alu_1_out));
  // memory_main main_1: pin names not known; wires that end beside it: alu_1_out, WE, regfile_1_r2, CLK, main_1_p5
  ControlDeALU controldealu_1 (.F3(Instruction[14:12]), .F7(Instruction[31:25]), .OPCODE(Instruction[6:0]), .op(op));
  Multiplexer #(.width(32), .enable("false")) multiplexer_3 (
    .in0(alu_1_out), .in1(main_1_p5), .out(multiplexer_3_out), .sel(MEMSEL));

  // Other names for the same wires on the sheet: fetch_addr[31:0] = PC; INST[31:0] = Instruction;
  //   OPCODE[6:0] = Instruction[6:0]; RD[4:0] = Instruction[11:7]; F3[2:0] = Instruction[14:12];
  //   RS1[4:0] = Instruction[19:15]; RS2[4:0] = Instruction[24:20]; F7[6:0] = Instruction[31:25]

  // Notes on the sheet:
  //   NOTE
  //   Please do not modify/replace/move/change/delete/etc input and output pins
  //   GeneradorIMM
  //   Control
  //   Control ALU
  //   These are debug/test outputs from your circuit
endmodule

module GeneradorImm (
  input  [31:0] INST,
  input  [6:0] Opcode,
  output [31:0] Imm
);

  wire comparator_1_eq, comparator_2_eq, comparator_3_eq, comparator_4_eq, comparator_5_eq, comparator_6_eq,
       comparator_7_eq, comparator_8_eq, or_1_out, or_2_out;
  wire [2:0] and_1_out, and_2_out, and_3_out, and_4_out, and_5_out, bit_extender_5_out, bit_extender_6_out,
       bit_extender_7_out, bit_extender_8_out, bit_extender_9_out, SEL;
  wire [31:0] TIPO_B, TIPO_I, TIPO_J, TIPO_S;

  // Probe on SEL
  Multiplexer #(.select(3), .width(32), .enable("false")) multiplexer_1 (
    .in1(TIPO_I), .in2(TIPO_S), .in3(TIPO_B), .in4({INST[31:12], {12{1'b0}}}), .in5(TIPO_J), .out(Imm),
    .sel(SEL));  // open: in0, in6, in7
  assign TIPO_I = {{20{INST[31]}}, INST[31:20]};  // Bit_Extender bit_extender_1
  assign TIPO_S = {{20{INST[31]}}, {INST[31:25], INST[11:7]}};  // Bit_Extender bit_extender_2
  assign TIPO_B = {{19{INST[31]}}, {INST[31], INST[7], INST[30:25], INST[11:8], 1'b0}};  // Bit_Extender bit_extender_3
  assign TIPO_J = {{11{INST[31]}}, {INST[31], INST[19:12], INST[20], INST[30:21], 1'b0}};  // Bit_Extender bit_extender_4
  Comparator #(.width(7), .mode("unsigned")) comparator_1 (
    .a(Opcode), .b(7'b0000011), .eq(comparator_1_eq));  // open: gt, lt
  Comparator #(.width(7), .mode("unsigned")) comparator_2 (
    .a(Opcode), .b(7'b0010011), .eq(comparator_2_eq));  // open: gt, lt
  Comparator #(.width(7), .mode("unsigned")) comparator_3 (
    .a(Opcode), .b(7'b1100111), .eq(comparator_3_eq));  // open: gt, lt
  Comparator #(.width(7), .mode("unsigned")) comparator_4 (
    .a(Opcode), .b(7'b0100011), .eq(comparator_4_eq));  // open: gt, lt
  Comparator #(.width(7), .mode("unsigned")) comparator_5 (
    .a(Opcode), .b(7'b1100011), .eq(comparator_5_eq));  // open: gt, lt
  Comparator #(.width(7), .mode("unsigned")) comparator_6 (
    .a(Opcode), .b(7'b0110111), .eq(comparator_6_eq));  // open: gt, lt
  or or_1 (or_1_out, comparator_6_eq, comparator_7_eq);
  Comparator #(.width(7), .mode("unsigned")) comparator_7 (
    .a(Opcode), .b(7'b0010111), .eq(comparator_7_eq));  // open: gt, lt
  Comparator #(.width(7), .mode("unsigned")) comparator_8 (
    .a(Opcode), .b(7'b1101111), .eq(comparator_8_eq));  // open: gt, lt
  assign bit_extender_5_out = {{2{1'b0}}, or_2_out};  // Bit_Extender bit_extender_5
  or or_2 (or_2_out, comparator_1_eq, comparator_2_eq, comparator_3_eq);
  assign bit_extender_6_out = {{2{1'b0}}, comparator_4_eq};  // Bit_Extender bit_extender_6
  assign bit_extender_7_out = {{2{1'b0}}, comparator_5_eq};  // Bit_Extender bit_extender_7
  assign bit_extender_8_out = {{2{1'b0}}, or_1_out};  // Bit_Extender bit_extender_8
  assign bit_extender_9_out = {{2{1'b0}}, comparator_8_eq};  // Bit_Extender bit_extender_9
  // Probe on and_1_out
  assign and_1_out = bit_extender_5_out & 3'b001;  // AND_Gate and_1, 3 bits wide
  // Probe on and_2_out
  assign and_2_out = bit_extender_6_out & 3'b010;  // AND_Gate and_2, 3 bits wide
  // Probe on and_3_out
  assign and_3_out = bit_extender_7_out & 3'b011;  // AND_Gate and_3, 3 bits wide
  // Probe on and_4_out
  assign and_4_out = bit_extender_8_out & 3'b100;  // AND_Gate and_4, 3 bits wide
  // Probe on and_5_out
  assign and_5_out = bit_extender_9_out & 3'b101;  // AND_Gate and_5, 3 bits wide
  // Probe on SEL
  assign SEL = and_1_out | and_2_out | and_3_out | and_4_out | and_5_out;  // OR_Gate or_3, 3 bits wide

  // Other names for the same wires on the sheet: TIPO_U[31:12] = INST[31:12]
endmodule

module Control (
  input  [6:0] Opcode,
  output RegW,
  output AluSel,
  output MemW,
  output MemR,
  output MemSel,
  output Branch,
  output Jump
);

  wire comparator_1_eq, comparator_2_eq, comparator_3_eq, comparator_4_eq, comparator_5_eq, comparator_6_eq,
       comparator_7_eq, comparator_8_eq, comparator_9_eq, comparator_10_eq, comparator_11_eq,
       comparator_15_eq, comparator_16_eq;

  Comparator #(.width(7), .mode("unsigned")) comparator_1 (
    .a(Opcode), .b(7'b0110011), .eq(comparator_1_eq));  // open: gt, lt
  Comparator #(.width(7), .mode("unsigned")) comparator_2 (
    .a(Opcode), .b(7'b0010011), .eq(comparator_2_eq));  // open: gt, lt
  Comparator #(.width(7), .mode("unsigned")) comparator_3 (
    .a(Opcode), .b(7'b0000011), .eq(comparator_3_eq));  // open: gt, lt
  Comparator #(.width(7), .mode("unsigned")) comparator_4 (
    .a(Opcode), .b(7'b0110111), .eq(comparator_4_eq));  // open: gt, lt
  Comparator #(.width(7), .mode("unsigned")) comparator_5 (
    .a(Opcode), .b(7'b0010111), .eq(comparator_5_eq));  // open: gt, lt
  Comparator #(.width(7), .mode("unsigned")) comparator_6 (
    .a(Opcode), .b(7'b1100111), .eq(comparator_6_eq));  // open: gt, lt
  Comparator #(.width(7), .mode("unsigned")) comparator_7 (
    .a(Opcode), .b(7'b1101111), .eq(comparator_7_eq));  // open: gt, lt
  or or_1 (RegW, comparator_1_eq, comparator_2_eq, comparator_3_eq, comparator_4_eq, comparator_5_eq, comparator_6_eq, comparator_7_eq);
  Comparator #(.width(7), .mode("unsigned")) comparator_8 (
    .a(Opcode), .b(7'b0010011), .eq(comparator_8_eq));  // open: gt, lt
  Comparator #(.width(7), .mode("unsigned")) comparator_9 (
    .a(Opcode), .b(7'b0000011), .eq(comparator_9_eq));  // open: gt, lt
  Comparator #(.width(7), .mode("unsigned")) comparator_10 (
    .a(Opcode), .b(7'b0100011), .eq(comparator_10_eq));  // open: gt, lt
  Comparator #(.width(7), .mode("unsigned")) comparator_11 (
    .a(Opcode), .b(7'b1100111), .eq(comparator_11_eq));  // open: gt, lt
  or or_2 (AluSel, comparator_8_eq, comparator_9_eq, comparator_10_eq, comparator_11_eq);
  Comparator #(.width(7), .mode("unsigned")) comparator_12 (.a(Opcode), .b(7'b0100011), .eq(MemW));  // open: gt, lt
  Comparator #(.width(7), .mode("unsigned")) comparator_13 (.a(Opcode), .b(7'b0000011), .eq(MemR));  // open: gt, lt
  Comparator #(.width(7), .mode("unsigned")) comparator_14 (.a(Opcode), .b(7'b1100011), .eq(Branch));  // open: gt, lt
  Comparator #(.width(7), .mode("unsigned")) comparator_15 (
    .a(Opcode), .b(7'b0100011), .eq(comparator_15_eq));  // open: gt, lt
  Comparator #(.width(7), .mode("unsigned")) comparator_16 (
    .a(Opcode), .b(7'b0100011), .eq(comparator_16_eq));  // open: gt, lt
  or or_3 (Jump, comparator_15_eq, comparator_16_eq);

  assign MemSel = MemR;
endmodule

module ControlDeALU (
  input  [2:0] F3,
  input  [6:0] F7,
  input  [6:0] OPCODE,
  output [3:0] op
);

  wire and_1_out, and_2_out, and_3_out, and_4_out, and_5_out, and_6_out, and_7_out, and_8_out, and_9_out,
       and_10_out, and_11_out, and_12_out, comparator_1_eq, comparator_2_eq, comparator_3_eq,
       comparator_4_eq, comparator_5_eq, comparator_6_eq, comparator_7_eq, comparator_8_eq, comparator_9_eq,
       comparator_10_eq, comparator_11_eq, comparator_12_eq, comparator_13_eq, comparator_14_eq,
       comparator_15_eq, comparator_16_eq, comparator_17_eq, comparator_18_eq, comparator_19_eq,
       comparator_20_eq, comparator_21_eq, comparator_22_eq, comparator_23_eq, comparator_24_eq,
       comparator_25_eq, comparator_26_eq, comparator_27_eq, comparator_28_eq, comparator_29_eq,
       comparator_30_eq, comparator_31_eq, comparator_32_eq, comparator_33_eq, comparator_34_eq,
       comparator_35_eq, comparator_36_eq;
  wire [2:0] and_25_out, bit_extender_13_out;
  wire [3:0] and_13_out, and_14_out, and_15_out, and_16_out, and_17_out, and_18_out, and_19_out, and_20_out,
       and_21_out, and_22_out, and_23_out, and_24_out, bit_extender_1_out, bit_extender_2_out,
       bit_extender_3_out, bit_extender_4_out, bit_extender_5_out, bit_extender_6_out, bit_extender_7_out,
       bit_extender_8_out, bit_extender_9_out, bit_extender_10_out, bit_extender_11_out, bit_extender_12_out,
       SEL;

  Comparator #(.width(3)) comparator_1 (.a(F3), .b(3'b001), .eq(comparator_1_eq));  // open: gt, lt
  Comparator #(.width(7)) comparator_2 (.a(F7), .b({7{1'b0}}), .eq(comparator_2_eq));  // open: gt, lt
  // Probe on 7'b0100000
  Comparator #(.width(7)) comparator_3 (.a(OPCODE), .b(7'b0110011), .eq(comparator_3_eq));  // open: gt, lt
  Comparator #(.width(7)) comparator_4 (.a(OPCODE), .b(7'b0110011), .eq(comparator_4_eq));  // open: gt, lt
  Comparator #(.width(3)) comparator_5 (.a(F3), .b(3'b101), .eq(comparator_5_eq));  // open: gt, lt
  Comparator #(.width(7)) comparator_6 (.a(F7), .b({7{1'b0}}), .eq(comparator_6_eq));  // open: gt, lt
  Comparator #(.width(7)) comparator_7 (.a(OPCODE), .b(7'b0110011), .eq(comparator_7_eq));  // open: gt, lt
  Comparator #(.width(3)) comparator_8 (.a(F3), .b(3'b000), .eq(comparator_8_eq));  // open: gt, lt
  Comparator #(.width(7)) comparator_9 (.a(F7), .b({7{1'b0}}), .eq(comparator_9_eq));  // open: gt, lt
  Comparator #(.width(7)) comparator_10 (.a(OPCODE), .b(7'b0110011), .eq(comparator_10_eq));  // open: gt, lt
  Comparator #(.width(3)) comparator_11 (.a(F3), .b(3'b110), .eq(comparator_11_eq));  // open: gt, lt
  Comparator #(.width(7)) comparator_12 (.a(F7), .b(7'b0000001), .eq(comparator_12_eq));  // open: gt, lt
  Comparator #(.width(7)) comparator_13 (.a(OPCODE), .b(7'b0110011), .eq(comparator_13_eq));  // open: gt, lt
  Comparator #(.width(3)) comparator_14 (.a(F3), .b(3'b111), .eq(comparator_14_eq));  // open: gt, lt
  Comparator #(.width(7)) comparator_15 (.a(F7), .b({7{1'b0}}), .eq(comparator_15_eq));  // open: gt, lt
  Comparator #(.width(7)) comparator_16 (.a(OPCODE), .b(7'b0110011), .eq(comparator_16_eq));  // open: gt, lt
  Comparator #(.width(3)) comparator_17 (.a(F3), .b(3'b110), .eq(comparator_17_eq));  // open: gt, lt
  Comparator #(.width(7)) comparator_18 (.a(F7), .b({7{1'b0}}), .eq(comparator_18_eq));  // open: gt, lt
  Comparator #(.width(7)) comparator_19 (.a(OPCODE), .b(7'b0110011), .eq(comparator_19_eq));  // open: gt, lt
  Comparator #(.width(3)) comparator_20 (.a(F3), .b(3'b001), .eq(comparator_20_eq));  // open: gt, lt
  Comparator #(.width(7)) comparator_21 (.a(F7), .b({7{1'b0}}), .eq(comparator_21_eq));  // open: gt, lt
  Comparator #(.width(7)) comparator_22 (.a(OPCODE), .b(7'b0110011), .eq(comparator_22_eq));  // open: gt, lt
  Comparator #(.width(3)) comparator_23 (.a(F3), .b(3'b100), .eq(comparator_23_eq));  // open: gt, lt
  Comparator #(.width(7)) comparator_24 (.a(F7), .b(7'b0000001), .eq(comparator_24_eq));  // open: gt, lt
  Comparator #(.width(7)) comparator_25 (.a(OPCODE), .b(7'b0110011), .eq(comparator_25_eq));  // open: gt, lt
  Comparator #(.width(3)) comparator_26 (.a(F3), .b(3'b110), .eq(comparator_26_eq));  // open: gt, lt
  Comparator #(.width(7)) comparator_27 (.a(F7), .b(7'b0100000), .eq(comparator_27_eq));  // open: gt, lt
  Comparator #(.width(7)) comparator_28 (.a(OPCODE), .b(7'b0110011), .eq(comparator_28_eq));  // open: gt, lt
  Comparator #(.width(3)) comparator_29 (.a(F3), .b(3'b010), .eq(comparator_29_eq));  // open: gt, lt
  Comparator #(.width(7)) comparator_30 (.a(F7), .b({7{1'b0}}), .eq(comparator_30_eq));  // open: gt, lt
  Comparator #(.width(7)) comparator_31 (.a(OPCODE), .b(7'b0110011), .eq(comparator_31_eq));  // open: gt, lt
  Comparator #(.width(3)) comparator_32 (.a(F3), .b(3'b000), .eq(comparator_32_eq));  // open: gt, lt
  Comparator #(.width(7)) comparator_33 (.a(F7), .b(7'b0000001), .eq(comparator_33_eq));  // open: gt, lt
  Comparator #(.width(7)) comparator_34 (.a(OPCODE), .b(7'b0110011), .eq(comparator_34_eq));  // open: gt, lt
  Comparator #(.width(3)) comparator_35 (.a(F3), .b(3'b001), .eq(comparator_35_eq));  // open: gt, lt
  Comparator #(.width(7)) comparator_36 (.a(F7), .b(7'b0000001), .eq(comparator_36_eq));  // open: gt, lt
  and and_1 (and_1_out, comparator_3_eq, comparator_1_eq, comparator_2_eq);
  and and_2 (and_2_out, comparator_4_eq, comparator_5_eq, comparator_6_eq);
  and and_3 (and_3_out, comparator_7_eq, comparator_8_eq, comparator_9_eq);
  and and_4 (and_4_out, comparator_10_eq, comparator_11_eq, comparator_12_eq);
  and and_5 (and_5_out, comparator_13_eq, comparator_14_eq, comparator_15_eq);
  and and_6 (and_6_out, comparator_16_eq, comparator_17_eq, comparator_18_eq);
  and and_7 (and_7_out, comparator_19_eq, comparator_20_eq, comparator_21_eq);
  and and_8 (and_8_out, comparator_22_eq, comparator_23_eq, comparator_24_eq);
  and and_9 (and_9_out, comparator_25_eq, comparator_26_eq, comparator_27_eq);
  and and_10 (and_10_out, comparator_28_eq, comparator_29_eq, comparator_30_eq);
  and and_11 (and_11_out, comparator_31_eq, comparator_32_eq, comparator_33_eq);
  // Probe on and_12_out
  and and_12 (and_12_out, comparator_34_eq, comparator_35_eq, comparator_36_eq);
  assign bit_extender_1_out = {{3{1'b0}}, and_1_out};  // Bit_Extender bit_extender_1
  assign bit_extender_2_out = {{3{1'b0}}, and_2_out};  // Bit_Extender bit_extender_2
  assign bit_extender_3_out = {{3{1'b0}}, and_3_out};  // Bit_Extender bit_extender_3
  assign bit_extender_4_out = {{3{1'b0}}, and_4_out};  // Bit_Extender bit_extender_4
  assign bit_extender_5_out = {{3{1'b0}}, and_5_out};  // Bit_Extender bit_extender_5
  assign bit_extender_6_out = {{3{1'b0}}, and_6_out};  // Bit_Extender bit_extender_6
  assign bit_extender_7_out = {{3{1'b0}}, and_7_out};  // Bit_Extender bit_extender_7
  assign bit_extender_8_out = {{3{1'b0}}, and_8_out};  // Bit_Extender bit_extender_8
  assign bit_extender_9_out = {{3{1'b0}}, and_9_out};  // Bit_Extender bit_extender_9
  assign bit_extender_10_out = {{3{1'b0}}, and_10_out};  // Bit_Extender bit_extender_10
  assign bit_extender_11_out = {{3{1'b0}}, and_11_out};  // Bit_Extender bit_extender_11
  // Probe on bit_extender_12_out
  assign bit_extender_12_out = {{3{1'b0}}, and_12_out};  // Bit_Extender bit_extender_12
  // Probe on 4'b1001
  assign and_13_out = bit_extender_1_out & 4'b0001;  // AND_Gate and_13, 4 bits wide
  assign and_14_out = bit_extender_2_out & 4'b0010;  // AND_Gate and_14, 4 bits wide
  assign and_15_out = bit_extender_11_out & 4'b1000;  // AND_Gate and_15, 4 bits wide
  assign and_16_out = bit_extender_12_out & 4'b1001;  // AND_Gate and_16, 4 bits wide
  // Probe on and_13_out
  // Probe on and_14_out
  assign and_17_out = bit_extender_3_out & 4'b0011;  // AND_Gate and_17, 4 bits wide
  assign and_18_out = bit_extender_4_out & 4'b1011;  // AND_Gate and_18, 4 bits wide
  assign and_19_out = bit_extender_5_out & 4'b0100;  // AND_Gate and_19, 4 bits wide
  assign and_20_out = bit_extender_6_out & 4'b0101;  // AND_Gate and_20, 4 bits wide
  assign and_21_out = bit_extender_7_out & 4'b0110;  // AND_Gate and_21, 4 bits wide
  assign and_22_out = bit_extender_8_out & 4'b1010;  // AND_Gate and_22, 4 bits wide
  assign and_23_out = bit_extender_9_out & 4'b1100;  // AND_Gate and_23, 4 bits wide
  assign and_24_out = bit_extender_10_out & 4'b0111;  // AND_Gate and_24, 4 bits wide
  // Probe on and_15_out
  // Probe on and_16_out
  // Probe on and_17_out
  assign SEL = and_13_out | and_14_out | and_17_out | and_18_out | and_19_out | and_20_out | and_21_out | and_22_out | and_23_out | and_24_out | and_15_out | and_16_out;  // OR_Gate or_1, 4 bits wide
  // Probe on bit_extender_13_out
  assign bit_extender_13_out = {{2{1'b0}}, 1'b1};  // Bit_Extender bit_extender_13
  // Probe on 3'b111
  // Probe on and_25_out
  assign and_25_out = bit_extender_13_out & 3'b111;  // AND_Gate and_25, 3 bits wide
  Multiplexer #(.select(4), .width(4), .enable("false")) multiplexer_1 (
    .in1(4'b0000), .in2(4'b0001), .in3(4'b0010), .in4(4'b0011), .in5(4'b0100), .in6(4'b0101), .in7(4'b0110),
    .in8(4'b0111), .in9(4'b1000), .in10(4'b1001), .in11(4'b1010), .in12(4'b1011), .out(op), .sel(SEL));  // open: in0, in13, in14, in15
endmodule
