// Logisim project regfile.circ as structural Verilog: 1 circuit, main circuit RegFile
module RegFile (
  input  [4:0] RD,
  input  [4:0] RS1,
  input  [4:0] RS2,
  input  [31:0] W,
  input  WE,
  input  Clk,
  output [31:0] s0,
  output [31:0] s1,
  output [31:0] t0,
  output [31:0] t1,
  output [31:0] a0,
  output [31:0] ra,
  output [31:0] sp,
  output [31:0] R1,
  output [31:0] R2
);

  wire and_1_out, and_2_out, and_3_out, and_4_out, and_5_out, and_6_out, and_7_out, comparator_1_eq,
       comparator_2_eq, comparator_3_eq, comparator_4_eq, comparator_5_eq, comparator_6_eq, comparator_7_eq;
  wire [31:0] a0_mux, ra_mux, s0_mux, s1_mux, sp_mux, t0_mux, t1_mux, zero;

  Comparator #(.width(5)) comparator_1 (.a(RD), .b(5'b00001), .eq(comparator_1_eq));  // open: gt, lt
  Register #(.width(32)) x1 (.D(W), .en(and_1_out), .Q(ra_mux), .clk(Clk));  // open: clr
  and and_1 (and_1_out, WE, comparator_1_eq);
  Multiplexer #(.select(5), .width(32), .enable("false")) multiplexer_1 (
    .in0(zero), .in1(ra_mux), .in2(sp_mux), .in5(t0_mux), .in6(t1_mux), .in8(s0_mux), .in9(s1_mux),
    .in10(a0_mux), .out(R1), .sel(RS1));  // open: in3, in4, in7, in11, in12, in13, in14, in15, in16, in17, in18, in19, in20, in21, in22, in23, in24, in25, in26, in27, in28, in29, in30, in31
  Register #(.width(32)) x6 (.D({32{1'b0}}), .en(WE), .Q(zero), .clk(Clk));  // open: clr
  Comparator #(.width(5)) comparator_2 (.a(RD), .b(5'b00010), .eq(comparator_2_eq));  // open: gt, lt
  Register #(.width(32)) x2 (.D(W), .en(and_2_out), .Q(sp_mux), .clk(Clk));  // open: clr
  and and_2 (and_2_out, WE, comparator_2_eq);
  Multiplexer #(.select(5), .width(32), .enable("false")) multiplexer_2 (
    .in0(zero), .in1(ra_mux), .in2(sp_mux), .in5(t0_mux), .in6(t1_mux), .in8(s0_mux), .in9(s1_mux),
    .in10(a0_mux), .out(R2), .sel(RS2));  // open: in3, in4, in7, in11, in12, in13, in14, in15, in16, in17, in18, in19, in20, in21, in22, in23, in24, in25, in26, in27, in28, in29, in30, in31
  Comparator #(.width(5)) comparator_3 (.a(RD), .b(5'b00101), .eq(comparator_3_eq));  // open: gt, lt
  and and_3 (and_3_out, WE, comparator_3_eq);
  Register #(.width(32)) x5 (.D(W), .en(and_3_out), .Q(t0_mux), .clk(Clk));  // open: clr
  Comparator #(.width(5)) comparator_4 (.a(RD), .b(5'b00110), .eq(comparator_4_eq));  // open: gt, lt
  Comparator #(.width(5)) comparator_5 (.a(RD), .b(5'b01000), .eq(comparator_5_eq));  // open: gt, lt
  Comparator #(.width(5)) comparator_6 (.a(RD), .b(5'b01001), .eq(comparator_6_eq));  // open: gt, lt
  Comparator #(.width(5)) comparator_7 (.a(RD), .b(5'b01010), .eq(comparator_7_eq));  // open: gt, lt
  and and_4 (and_4_out, WE, comparator_4_eq);
  and and_5 (and_5_out, WE, comparator_5_eq);
  and and_6 (and_6_out, WE, comparator_6_eq);
  and and_7 (and_7_out, WE, comparator_7_eq);
  Register #(.width(32)) x6_2 (.D(W), .en(and_4_out), .Q(t1_mux), .clk(Clk));  // open: clr
  Register #(.width(32)) x8 (.D(W), .en(and_5_out), .Q(s0_mux), .clk(Clk));  // open: clr
  Register #(.width(32)) x9 (.D(W), .en(and_6_out), .Q(s1_mux), .clk(Clk));  // open: clr
  Register #(.width(32)) x10 (.D(W), .en(and_7_out), .Q(a0_mux), .clk(Clk));  // open: clr

  // Notes on the sheet:
  //   Write Register
  //   Read Register 1
  //   Read Register 2
  //   Write Data
  //   Write Enable
  //   Clock
  //   NOTE
  //   Please do not modify/replace/move/change/delete/etc input and output pins
  //   These are debug/test outputs from your circuit
  //   Read Data 1
  //   Read Data 2
endmodule
